// Logisim project ADE8v1.1.circ as structural Verilog: 7 circuits, main circuit Test
module Test (
  input  Run,
  input  in_2,
  input  in_3,
  input  in_4,
  input  in_5,
  input  in_6,
  input  in_7,
  input  in_8,
  input  in_9
);

  wire ade8_1_read, ade8_1_write, clock_1_out, comparator_1_eq, io_chipselect_1_output,
       io_chipselect_2_output, io_chipselect_3_output, io_chipselect_4_output, io_chipselect_5_output,
       io_chipselect_6_output, io_chipselect_7_output, iostatusregister_1_newdataflag, New_data_out,
       not_1_out, or_1_out, Reset_out, Step_out;
  wire [0:0] keyboard_1_avail;
  wire [3:0] ade8_1_flag, register_1_q, tickcounter_1_c, tickcounter_1_d, tickcounter_1_m, tickcounter_1_u;
  wire [6:0] keyboard_1_data;
  wire [7:0] ade8_1_acc, ade8_1_addr_bus, ade8_1_data_bus_out, ade8_1_iro, ade8_1_irp, ade8_1_pc, ade8_1_sp,
       iostatusregister_1_statusregister, ram_1_data;
  wire [7:4] register_1_q_2;

  Button Step (.out(Step_out));
  Clock clock_1 (.out(clock_1_out));
  Button Reset (.out(Reset_out));
  or or_1 (or_1_out, Run, Step_out);
  // Probe on ade8_1_acc
  // Probe on ade8_1_iro
  // Probe on ade8_1_pc
  // Probe on ade8_1_sp
  // Probe on ade8_1_irp
  // Probe on ade8_1_flag
  // Probe on ade8_1_addr_bus
  // Probe on ram_1_data
  ADE8 ade8_1 (
    .Clock(clock_1_out), .Step(or_1_out), .DATA_BUS_IN(ram_1_data), .Read(ade8_1_read),
    .DATA_BUS_OUT(ade8_1_data_bus_out), .ADDR_BUS(ade8_1_addr_bus), .PC(ade8_1_pc), .Reset(Reset_out),
    .FLAG(ade8_1_flag), .ACC(ade8_1_acc), .SP(ade8_1_sp), .IRP(ade8_1_irp), .IRO(ade8_1_iro),
    .Write(ade8_1_write));
  // Probe on ade8_1_data_bus_out
  not not_1 (not_1_out, comparator_1_eq);
  Comparator #(.width(4)) comparator_1 (.a(4'b1101), .b(ade8_1_addr_bus[7:4]), .eq(comparator_1_eq));  // open: gt, lt
  IO_ChipSelect io_chipselect_1 (
    .Input(ade8_1_read), .AddrBus(ade8_1_addr_bus), .IOPort(4'b0010), .Output(io_chipselect_1_output),
    .I_O(comparator_1_eq));
  IO_ChipSelect io_chipselect_2 (
    .Input(ade8_1_read), .AddrBus(ade8_1_addr_bus), .IOPort(4'b0011), .Output(io_chipselect_2_output),
    .I_O(comparator_1_eq));
  IO_ChipSelect io_chipselect_3 (
    .Input(ade8_1_write), .AddrBus(ade8_1_addr_bus), .IOPort(4'b0000), .Output(io_chipselect_3_output),
    .I_O(comparator_1_eq));
  IO_ChipSelect io_chipselect_4 (
    .Input(ade8_1_write), .AddrBus(ade8_1_addr_bus), .IOPort(4'b0001), .Output(io_chipselect_4_output),
    .I_O(comparator_1_eq));
  IO_ChipSelect io_chipselect_5 (
    .Input(ade8_1_write), .AddrBus(ade8_1_addr_bus), .IOPort(4'b0100), .Output(io_chipselect_5_output),
    .I_O(comparator_1_eq));
  IO_ChipSelect io_chipselect_6 (
    .Input(ade8_1_read), .AddrBus(ade8_1_addr_bus), .IOPort(4'b0101), .Output(io_chipselect_6_output),
    .I_O(comparator_1_eq));
  IO_ChipSelect io_chipselect_7 (
    .Input(ade8_1_read), .AddrBus(ade8_1_addr_bus), .IOPort(4'b0110), .Output(io_chipselect_7_output),
    .I_O(comparator_1_eq));
  RAM #(.bus("separate")) ram_1 (
    .addr(ade8_1_addr_bus), .din(ade8_1_data_bus_out), .data(ram_1_data), .str(ade8_1_write),
    .sel(not_1_out), .clk(clock_1_out), .ld(ade8_1_read));  // open: clr
  assign ram_1_data = io_chipselect_1_output ? {in_2, in_3, in_4, in_5, in_6, in_7, in_8, in_9} : 8'bz;  // Controlled_Buffer controlled_buffer_1
  assign ram_1_data = io_chipselect_2_output ? iostatusregister_1_statusregister : 8'bz;  // Controlled_Buffer controlled_buffer_2
  IOStatusRegister iostatusregister_1 (
    .Read(io_chipselect_1_output), .Clk(clock_1_out), .SetNewData(New_data_out), .Reset(Reset_out),
    .NewDataFlag(iostatusregister_1_newdataflag), .StatusRegister(iostatusregister_1_statusregister));  // open: InputEdgeFinder
  Register register_1 (
    .D(ade8_1_data_bus_out), .en(io_chipselect_3_output), .Q({register_1_q_2, register_1_q}),
    .clk(clock_1_out), .clr(Reset_out));
  TickCounter tickcounter_1 (
    .DataIn(ade8_1_data_bus_out), .Wr(io_chipselect_5_output), .Clock(clock_1_out), .Reset(Reset_out),
    .U(tickcounter_1_u), .D(tickcounter_1_d), .C(tickcounter_1_c), .M(tickcounter_1_m));
  Keyboard keyboard_1 (
    .clk(clock_1_out), .re(io_chipselect_6_output), .clr(Reset_out), .avail(keyboard_1_avail[0]),
    .data(keyboard_1_data));
  Hex_Digit_Display hex_digit_display_1 (.value(register_1_q_2));  // open: dp
  TTY #(.rows(2), .cols(16)) tty_1 (
    .data(ade8_1_data_bus_out[6:0]), .clk(clock_1_out), .we(io_chipselect_4_output), .clr(Reset_out));
  Hex_Digit_Display hex_digit_display_2 (.value(tickcounter_1_m));  // open: dp
  Hex_Digit_Display hex_digit_display_3 (.value(tickcounter_1_c));  // open: dp
  Hex_Digit_Display hex_digit_display_4 (.value(register_1_q));  // open: dp
  Hex_Digit_Display hex_digit_display_5 (.value(tickcounter_1_u));  // open: dp
  Hex_Digit_Display hex_digit_display_6 (.value(tickcounter_1_d));  // open: dp
  Button New_data (.out(New_data_out));
  LED led_1 (.in(iostatusregister_1_newdataflag));
  assign ram_1_data = io_chipselect_6_output ? {1'b0, keyboard_1_data} : 8'bz;  // Controlled_Buffer controlled_buffer_3
  assign ram_1_data = io_chipselect_7_output ? {{7{1'b0}}, keyboard_1_avail[0]} : 8'bz;  // Controlled_Buffer controlled_buffer_4

  // Notes on the sheet:
  //   CONZ
  //   ADE to Addr bus
  //   MemIO to ADE
  //    data bus
  //   ADE to MemIO
  //    data bus
  //   Mem/IO selection
  //   MEMORIA
  //   Read register
  //   Status register
  //   Read register
  //   Status register
  //   ADE8: Architettura di Esempio a 8 bit
  //   v1.1 (29/09/2023)
  //   INPUT: Pannello a 8 bit
  //   INPUT: Tastiera
  //   OUTPUT: 7seg
  //   OUTPUT: LCD
  //   UTILITY: tic Counter
endmodule

module ALU1bit (
  input  A,
  input  B,
  input  Cin,
  input  [1:0] S,
  output Out,
  output Cout
);

  wire adder_1_out, and_1_out, or_1_out, xor_1_out;

  xor xor_1 (xor_1_out, B, S[0]);
  and and_1 (and_1_out, A, B);
  or or_1 (or_1_out, A, B);
  Adder #(.width(1)) adder_1 (.a(A), .b(xor_1_out), .out(adder_1_out), .cin(Cin), .cout(Cout));
  Multiplexer #(.select(2), .enable("false")) multiplexer_1 (
    .in0(and_1_out), .in1(or_1_out), .in2(adder_1_out), .in3(adder_1_out), .out(Out), .sel(S));
endmodule

module ALU8bit (
  input  [7:0] A,
  input  [7:0] B,
  input  [1:0] S,
  input  Cin,
  output [7:0] Out,
  output [3:0] Flag
);

  wire alu1bit_1_cout, alu1bit_2_cout, alu1bit_3_cout, alu1bit_4_cout, alu1bit_5_cout, alu1bit_6_cout,
       alu1bit_7_cout;

  ALU1bit alu1bit_1 (.A(A[0]), .B(B[0]), .Cin(Cin), .S(S), .Out(Out[0]), .Cout(alu1bit_1_cout));
  ALU1bit alu1bit_2 (.A(A[1]), .B(B[1]), .Cin(alu1bit_1_cout), .S(S), .Out(Out[1]), .Cout(alu1bit_2_cout));
  ALU1bit alu1bit_3 (.A(A[2]), .B(B[2]), .Cin(alu1bit_2_cout), .S(S), .Out(Out[2]), .Cout(alu1bit_3_cout));
  ALU1bit alu1bit_4 (.A(A[3]), .B(B[3]), .Cin(alu1bit_3_cout), .S(S), .Out(Out[3]), .Cout(alu1bit_4_cout));
  ALU1bit alu1bit_5 (.A(A[4]), .B(B[4]), .Cin(alu1bit_4_cout), .S(S), .Out(Out[4]), .Cout(alu1bit_5_cout));
  ALU1bit alu1bit_6 (.A(A[5]), .B(B[5]), .Cin(alu1bit_5_cout), .S(S), .Out(Out[5]), .Cout(alu1bit_6_cout));
  ALU1bit alu1bit_7 (.A(A[6]), .B(B[6]), .Cin(alu1bit_6_cout), .S(S), .Out(Out[6]), .Cout(alu1bit_7_cout));
  ALU1bit alu1bit_8 (.A(A[7]), .B(B[7]), .Cin(alu1bit_7_cout), .S(S), .Out(Flag[1]), .Cout(Flag[3]));
  Comparator comparator_1 (.a({Flag[1], Out[6:0]}), .b({8{1'b0}}), .eq(Flag[0]));  // open: gt, lt
  xor xor_1 (Flag[2], alu1bit_7_cout, Flag[3]);

  assign Out[7] = Flag[1];

  // Notes on the sheet:
  //   Z - Zero
  //   N - Negative
  //   O - Overflow
  //   C - Carry
endmodule

module ADE8 (
  input  Reset,
  input  Clock,
  input  [7:0] DATA_BUS_IN,
  input  Step,
  output [3:0] FLAG,
  output [7:0] SP,
  output [7:0] ACC,
  output [7:0] DATA_BUS_OUT,
  output Read,
  output Write,
  output [7:0] ADDR_BUS,
  output [7:0] PC,
  output [7:0] IRP,
  output [7:0] IRO
);

  wire ACCie, ACCoe, ALUAie, ALUOUTie, ALUOUToe, and_1_out, Cin, comparator_1_eq, FLAGie, IROie, IROoe,
       IRPie, IRPoe, MARie, MARoe, MDRie, MDRoe, multiplexer_5_out, not_1_out, or_1_out, or_2_out, PCie,
       PCoe, SPie, SPoe, xor_1_out, ZA;
  wire [1:0] S;
  wire [2:0] rom_2_data_2;
  wire [3:0] alu8bit_1_flag;
  wire [3:3] rom_2_data;
  wire [7:0] adder_1_out, alu8bit_1_out, ALUA_q, ALUout_q, controlled_buffer_1_out, multiplexer_1_out,
       multiplexer_2_out, multiplexer_3_out, multiplexer_4_out, rom_1_data, uPC_q;

  Register u_SP (.D(controlled_buffer_1_out), .en(SPie), .Q(SP), .clk(Clock), .clr(Reset));
  Register u_ACC (.D(controlled_buffer_1_out), .en(ACCie), .Q(ACC), .clk(Clock), .clr(Reset));
  Register MAR (.D(controlled_buffer_1_out), .en(MARie), .Q(ADDR_BUS), .clk(Clock));  // open: clr
  Register u_PC (.D(controlled_buffer_1_out), .en(PCie), .Q(PC), .clk(Clock), .clr(Reset));
  Register u_IRP (.D(controlled_buffer_1_out), .en(IRPie), .Q(IRP), .clk(Clock), .clr(Reset));
  assign controlled_buffer_1_out = IRPoe ? IRP : 8'bz;  // Controlled_Buffer controlled_buffer_1
  Register u_IRO (.D(controlled_buffer_1_out), .en(IROie), .Q(IRO), .clk(Clock), .clr(Reset));
  assign controlled_buffer_1_out = IROoe ? IRO : 8'bz;  // Controlled_Buffer controlled_buffer_2
  assign controlled_buffer_1_out = ALUOUToe ? ALUout_q : 8'bz;  // Controlled_Buffer controlled_buffer_3
  assign controlled_buffer_1_out = SPoe ? SP : 8'bz;  // Controlled_Buffer controlled_buffer_4
  assign controlled_buffer_1_out = ACCoe ? ACC : 8'bz;  // Controlled_Buffer controlled_buffer_5
  Multiplexer #(.width(8), .enable("false")) multiplexer_1 (
    .in0(controlled_buffer_1_out), .in1(DATA_BUS_IN), .out(multiplexer_1_out), .sel(Read));
  assign controlled_buffer_1_out = PCoe ? PC : 8'bz;  // Controlled_Buffer controlled_buffer_6
  Register ALUA (.D(controlled_buffer_1_out), .en(ALUAie), .Q(ALUA_q), .clk(Clock), .clr(Reset));
  Register MDR (.D(multiplexer_1_out), .en(or_1_out), .Q(DATA_BUS_OUT), .clk(Clock));  // open: clr
  or or_1 (or_1_out, Read, MDRie);
  Multiplexer #(.width(8), .enable("false")) multiplexer_2 (
    .in0({8{1'b0}}), .in1(ALUA_q), .out(multiplexer_2_out), .sel(ZA));
  assign controlled_buffer_1_out = MDRoe ? DATA_BUS_OUT : 8'bz;  // Controlled_Buffer controlled_buffer_7
  ROM rom_1 (.addr(IRO), .data(rom_1_data));  // open: sel
  ALU8bit alu8bit_1 (
    .A(multiplexer_2_out), .B(controlled_buffer_1_out), .S(S), .Cin(Cin), .Out(alu8bit_1_out),
    .Flag(alu8bit_1_flag));
  Multiplexer #(.width(8), .enable("false")) multiplexer_3 (
    .in0({8{1'b0}}), .in1(adder_1_out), .out(multiplexer_3_out), .sel(and_1_out));
  Adder adder_1 (.a(uPC_q), .b(8'h1), .out(adder_1_out));  // open: cin, cout
  and and_1 (and_1_out, or_2_out, multiplexer_5_out);
  or or_2 (or_2_out, Step, ~comparator_1_eq);  // OR_Gate
  Multiplexer #(.width(8), .enable("false")) multiplexer_4 (
    .in0(multiplexer_3_out), .in1(rom_1_data), .out(multiplexer_4_out), .sel(rom_2_data[3]));
  Register ALUout (.D(alu8bit_1_out), .en(ALUOUTie), .Q(ALUout_q), .clk(Clock));  // open: clr
  Register #(.width(4)) u_FLAG (.D(alu8bit_1_flag), .en(FLAGie), .Q(FLAG), .clk(Clock), .clr(Reset));
  Register uPC (.D(multiplexer_4_out), .Q(uPC_q), .clk(Clock), .clr(Reset));  // open: en
  Comparator #(.mode("unsigned")) comparator_1 (.a(uPC_q), .b({8{1'b0}}), .eq(comparator_1_eq));  // open: gt, lt
  ROM #(.dataWidth(28)) rom_2 (
    .addr(uPC_q),
    .data({IROie, IROoe, IRPie, IRPoe, PCie, PCoe, MARie, MARoe, MDRie, MDRoe, Read, Write, ACCie, ACCoe, SPie, SPoe, ALUOUTie, ALUOUToe, ALUAie, FLAGie, ZA, S, Cin, rom_2_data[3], rom_2_data_2}));  // open: sel
  Multiplexer #(.select(3), .enable("false")) multiplexer_5 (
    .in0(1'b0), .in1(1'b1), .in2(FLAG[0]), .in3(FLAG[1]), .in4(FLAG[2]), .in5(FLAG[3]), .in6(not_1_out),
    .in7(xor_1_out), .out(multiplexer_5_out), .sel(rom_2_data_2));
  not not_1 (not_1_out, FLAG[3]);
  xor xor_1 (xor_1_out, FLAG[1], FLAG[2]);

  // Other names for the same wires on the sheet: MDRbusoe = Write; MDRbusie = Read

  // Notes on the sheet:
  //   CLK
  //   BUS interno
  //   Decodifica dell'opcode
  //   contents of rom_1 (hex, n*v repeats v):
  //   18 9 2a 4a 71 11*0 1a 0 2e 4f 78 11*0 1c a 32 54 7f 11*0 1f d 37 5a 87 11*0 22 10 3c 60 8f 11*0 25
  //   13 41 66 97 11*0 28 16 46 6c 9f 11*0 5 7 14*0 a6 ab b7 bc ae b1 b4 9*0 bf c0 c2 c4 c6 ca c8
  //   ROM con il microcodice
  //   contents of rom_2 (hex, n*v repeats v):
  //   600851 a20c51 8060001 800401 2240008 4971 8400 4961 8400 1008000 4201 1000981 8400 4201 10009a1 8400
  //   4201 10009c1 8400 4201 10009f1 8400 4201 10009f0 20001 48000 84001 10000 24201 40981 8400 24201
  //   409a1 8400 24201 409c1 8400 24201 409f1 8400 24201 409f0 20001 240001 20001 48000 20001 240001 84001
  //   10000 20001 240001 24201 40981 8400 20001 240001 24201 409a1 8400 20001 240001 24201 409c1 8400
  //   20001 240001 24201 409f1 8400 20001 240001 24201 409f0 1201 10008c1 200401 20001 48000 1201 10008c1
  //   200401 84001 10000 1201 10008c1 200401 24201 40981 8400 1201 10008c1 200401 24201 409a1 8400 1201
  //   10008c1 200401 24201 409c1 8400 1201 10008c1 200401 24201 409f1 8400 1201 10008c1 200401 24201 409f0
  //   1201 10008c1 200401 20001 240001 20001 48000 1201 10008c1 200401 20001 240001 84001 10000 1201
  //   10008c1 200401 20001 240001 24201 40981 8400 1201 10008c1 200401 20001 240001 24201 409a1 8400 1201
  //   10008c1 200401 20001 240001 24201 409c1 8400 1201 10008c1 200401 20001 240001 24201 409f1 8400 1201
  //   10008c1 200401 20001 240001 24201 409f0 1a01 ce1 202401 84001 10000 201851 22401 48000 1201 10008f1
  //   2400 1201 10008c1 2400 1201 10008c1 8400 1a01 ce1 202401 480001 1810000 201851 22401 840000 1800000
  //   2 1800000 3 1800000 4 1800000 5 1800000 6 1800000 7 1800000
endmodule

module IO_ChipSelect (
  input  Input,
  input  [7:0] AddrBus,
  input  [3:0] IOPort,
  input  I_O,
  output Output
);

  wire and_1_out, comparator_1_eq;

  Comparator #(.width(4), .mode("unsigned")) comparator_1 (
    .a(AddrBus[3:0]), .b(IOPort), .eq(comparator_1_eq));  // open: gt, lt
  and and_1 (and_1_out, comparator_1_eq, I_O);
  and and_2 (Output, Input, and_1_out);
endmodule

module IOStatusRegister (
  input  Read,
  input  Clk,
  input  SetNewData,
  input  Reset,
  output NewDataFlag,
  output InputEdgeFinder,
  output [7:0] StatusRegister
);

  wire and_2_out, d_ff_1_q, d_ff_2_q, not_1_out, not_2_out;

  D_Flip_Flop d_ff_1 (.clk(Clk), .D(SetNewData), .Q(d_ff_1_q));  // open: Qn, preset, en, reset
  D_Flip_Flop d_ff_2 (.clk(Clk), .D(d_ff_1_q), .Q(d_ff_2_q));  // open: Qn, preset, en, reset
  // Probe on d_ff_1_q
  // Probe on d_ff_2_q
  not not_1 (not_1_out, d_ff_2_q);
  not not_2 (not_2_out, Read);
  and and_1 (InputEdgeFinder, not_1_out, d_ff_1_q);
  and and_2 (and_2_out, not_2_out, InputEdgeFinder);
  S_R_Flip_Flop s_r_ff_1 (.S(and_2_out), .clk(Clk), .R(Read), .Q(NewDataFlag), .reset(Reset));  // open: Qn, preset, en

  assign StatusRegister = {{7{1'b0}}, NewDataFlag};
endmodule

module TickCounter (
  input  [7:0] DataIn,
  input  Wr,
  input  Clock,
  input  Reset,
  output [3:0] U,
  output [3:0] D,
  output [3:0] C,
  output [3:0] M
);

  wire [7:0] StatusRegister_q;
  wire [15:0] counter_1_q, divider_1_out, divider_2_out, divider_3_out;
  wire [15:4] divider_1_rem, divider_2_rem, divider_3_rem, divider_4_rem;

  Register StatusRegister (.D(DataIn), .en(Wr), .Q(StatusRegister_q), .clk(Clock));  // open: clr
  Counter #(.width(16), .max('hffff)) counter_1 (
    .count(StatusRegister_q[0]), .Q(counter_1_q), .clk(Clock), .clr(Reset));  // open: load, D, carry
  Divider #(.width(16)) divider_1 (
    .a(counter_1_q), .b(16'ha), .out(divider_1_out), .rem({divider_1_rem, U}));  // open: upper
  Divider #(.width(16)) divider_2 (
    .a(divider_1_out), .b(16'ha), .out(divider_2_out), .rem({divider_2_rem, D}));  // open: upper
  Divider #(.width(16)) divider_3 (
    .a(divider_2_out), .b(16'ha), .out(divider_3_out), .rem({divider_3_rem, C}));  // open: upper
  Divider #(.width(16)) divider_4 (.a(divider_3_out), .b(16'ha), .rem({divider_4_rem, M}));  // open: out, upper
endmodule
